# Fritzing sketch ALL 4 NODE MCU (s) IN A SINGLE BREAD BOARD VIEW (saved by Fritzing 0.9.3b)

parts:
  M1 = fc-51 [package=THT]
  M2 = fc-51 [package=THT]
  M3 = fc-51 [package=THT]
  M4 = fc-51 [package=THT]
  M5 = fc-51 [package=THT]
  M6 = fc-51 [package=THT]
  M7 = fc-51 [package=THT]
  M8 = fc-51 [package=THT]
  U1 = NodeMCU V1.0
  U2 = NodeMCU V1.0
  U3 = NodeMCU V1.0
  Bat1 = battery_holder_single_18650
  SIM800L1 = SIM800L
  U4 = NodeMCU V1.0
  A1 = NEO-6M GPS Module [part_number=GY-GPS6MV2]
  Vibration_Sensor_Module1 = Vibration Sensor Module [chip_label=?]
  e-radionica_com1 = LM393 LDR breakout [part_number=100027]
  MOTOR1 = Vibration Motor
  MOTOR2 = Vibration Motor
  MOTOR3 = Vibration Motor
  S1 = Round Pushbutton

nets:
  N1: M1.pin1, U2.D6
  N2: M1.pin3, M3.pin3, M4.pin3, U2.3V3
  N3: M2.pin1, U2.D5
  N4: M2.pin2, U2.GND
  N5: M2.pin3, U2.D0
  N6: M3.pin1, U2.D2
  N7: M4.pin1, U2.D7
  N8: M5.pin1, U1.D2
  N9: M5.pin3, U1.D0
  N10: M6.pin1, U1.D5
  N11: M6.pin3, M7.pin3, M8.pin3, U1.3V3
  N12: M7.pin1, U1.D7
  N13: M7.pin2, U1.GND
  N14: M8.pin1, U1.D6
  N15: U3.D1, Vibration_Sensor_Module1.DO
  N16: U3.D2, SIM800L1.TXD
  N17: U3.D3, SIM800L1.RXD
  VCC: U3.3V3, A1.Vcc, Vibration_Sensor_Module1.VCC, e-radionica_com1.VCC
  GND: U3.GND, Bat1.+#1, A1.GND, Vibration_Sensor_Module1.GND
  N18: U3.D5, A1.Tx
  N19: U3.D6, A1.Rx
  N20: U3.D7, e-radionica_com1.DO
  N21: Bat1.+#0, S1.leg0
  N22: SIM800L1.VCC, S1.leg1
  N23: U4.D2, MOTOR1.POS
  N24: U4.D3, MOTOR3.POS
  N25: U4.GND, MOTOR1.NEG
  N26: U4.D7, MOTOR2.POS

notes:
  RIGHT
  BOTTOM
  LEFT
  FRONT
  RIGHT1
  RIGHT2
  LEFT1
  LEFT2
  LEFT OBSTACLE SIGNALLER
  RIGHT OBSTACLE SIGNALLER
  FRONT OBSTACLE / PIT SIGNALLER

custom parts:
  NodeMCU V1.0: ESP8266 based NodeMCU
  battery_holder_single_18650: single 18650 battery holder
  SIM800L: SIM800L is a miniature cellular module which allows for GPRS transmission, sending and receiving SMS and making and receiving voice calls. Low cost and small footprint and quad band frequency support make this module perfect solution for any project that require long range connectivity. After connecting power module boots up, searches for cellular network and login automatically. On board LED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
  NEO-6M GPS Module: GY-GPS6MV2 NEO-6M GPS Module Module based on U-blox NEO-6M GPS engine, incorporating regulator for 3.3-5V DC input, MS621FE-compatible rechargeable battery for backup and EEPROM for storing configuration settings. Links: NEO-6 series product information page NEO-6 Datasheet
  Vibration Sensor Module: This Vibration Sensor use the SW-18015P from MEC to measure the vibration.It can triggerd from any angle, and often used for flex, touch, vibration and shock measurements. There is an on-board potentiometer to adjust the threshold of vibration.It outputs logic HIGH when this module not triggered while logic Low when triggered.
  Vibration Motor: An eccentric vibration motor!
